// Logisim project ABCdiode.circ as structural Verilog: 2 circuits, main circuit Display decode
module Display_decode (
  input  A,
  input  B,
  input  C,
  input  A_2,
  input  B_2,
  input  C_2,
  input  A_3,
  input  B_3,
  input  C_3
);

  wire and_1_out, and_2_out, and_3_out, and_4_out, and_5_out, nor_1_out, nor_2_out, not_1_out, not_2_out,
       not_3_out, not_4_out, not_5_out, not_6_out, not_7_out, not_8_out;

  not not_1 (not_1_out, A);
  not not_2 (not_2_out, B);
  not not_3 (not_3_out, B_2);
  not not_4 (not_4_out, C_2);
  not not_5 (not_5_out, A_3);
  not not_6 (not_6_out, C_3);
  not not_7 (not_7_out, C);
  and and_1 (and_1_out, not_1_out, not_2_out, C);
  and and_2 (and_2_out, not_2_out, not_7_out, A);
  and and_3 (and_3_out, A_2, C_2, not_3_out);
  and and_4 (and_4_out, A_2, B_2, not_4_out);
  and and_5 (and_5_out, not_5_out, B_3, not_6_out);
  nor nor_1 (nor_1_out, and_1_out, and_2_out);
  _7_Segment_Display u_7_segment_display_1 (.c(not_8_out));  // open: g, f, a, b, e, d, dp
  not not_8 (not_8_out, and_5_out);
  _7_Segment_Display u_7_segment_display_2 (.a(nor_1_out));  // open: g, f, b, e, d, c, dp
  nor nor_2 (nor_2_out, and_3_out, and_4_out);
  _7_Segment_Display u_7_segment_display_3 (.b(nor_2_out));  // open: g, f, a, e, d, c, dp

  // Notes on the sheet:
  //   C
  //   A
  //   B
  //   Krenemo inverznom logikom i izdvojimo slucajeve tj. cifre za koje taj deo segmenta NE TREBA da svetli
endmodule

module Counter (
  input  in_1
);

  wire clock_1_out;
  wire [7:0] adder_1_out, register_1_q;

  Adder adder_1 (.a(8'h1), .b(register_1_q), .out(adder_1_out));  // open: cin, cout
  Register register_1 (.D(adder_1_out), .en(in_1), .Q(register_1_q), .clk(clock_1_out));  // open: clr
  Clock clock_1 (.out(clock_1_out));
  // Probe on register_1_q
endmodule
