// Logisim project Z1.circ as structural Verilog: 1 circuit, main circuit main
module main (
  input  b2,
  input  b1,
  input  b0,
  input  a2,
  input  a1,
  input  a0,
  output out_7
);

  wire xor_1_out, xor_2_out, xor_3_out;

  xor xor_1 (xor_1_out, b2, a2);
  or or_1 (out_7, xor_1_out, xor_2_out, xor_3_out);
  xor xor_2 (xor_2_out, b1, a1);
  xor xor_3 (xor_3_out, b0, a0);
endmodule
