// Logisim project Z2.circ as structural Verilog: 1 circuit, main circuit main
module main (
  input  [1:0] b0,
  input  [1:0] a0,
  output out_3
);

  wire and_1_out, and_2_out, and_3_out, and_4_out, and_5_out, clock_1_out, not_1_out, not_2_out, not_3_out,
       not_4_out, or_1_out, or_2_out, or_3_out;
  wire [1:0] ax_q, bx_q;

  Clock clock_1 (.out(clock_1_out));
  Register #(.width(2)) ax (.D(a0), .Q(ax_q), .clk(clock_1_out));  // open: en, clr
  Register #(.width(2)) bx (.D(b0), .Q(bx_q), .clk(clock_1_out));  // open: en, clr
  not not_1 (not_1_out, ax_q[0]);
  not not_2 (not_2_out, ax_q[1]);
  and and_1 (and_1_out, not_1_out, ax_q[1]);
  and and_2 (and_2_out, ax_q[0], not_2_out);
  not not_3 (not_3_out, bx_q[0]);
  not not_4 (not_4_out, bx_q[1]);
  and and_3 (and_3_out, not_3_out, bx_q[1]);
  and and_4 (and_4_out, bx_q[0], not_4_out);
  or or_1 (or_1_out, and_1_out, and_2_out);
  or or_2 (or_2_out, and_3_out, and_4_out);
  and and_5 (and_5_out, or_1_out, or_2_out);
  or or_3 (or_3_out, or_2_out, or_1_out);
  and and_6 (out_3, and_5_out, or_3_out);
endmodule
